# Fritzing sketch schematic (saved by Fritzing 0.9.2b)
breadboards: 1

parts:
  U1 = ESP32S-30Pin [part_number=ESP32S-Generic]
  Componente1 = Real Time Clock Module - DS1307 RTC Breakout Board
  J1 = Piezo Speaker
  LED1 = LED - 5mm [color="Red (633nm)" package="5 mm [THT]"]
  Q1 = LTR-301 [package=ltr-301]
  D1 = LTE-302 [package=lte-302]
  R1 = Resistor [tolerance=±5% resistance=1M package=THT]
  R2 = Resistor [tolerance=±5% resistance=330 package=THT]
  S1 = Momentary Switch [package=ksa_sealed_tac_switch]
  R3 = Resistor [tolerance=±5% resistance=10k package="0603 [SMD]"]

nets:
  N1: U1.3.3, Componente1.5V, R1.Pin_0, S1.4
  N2: U1.GPIO32, Q1.E, R1.Pin_1
  N3: U1.GPIO33, D1.C
  N4: U1.GPIO26, S1.1, R3.Pin_0
  N5: U1.GPIO27, LED1.anode
  GND: U1.GND, Componente1.GND, J1.pin1, LED1.cathode, Q1.C, R2.Pin_1, R3.Pin_1
  N6: U1.GPIO15, J1.pin2
  N7: U1.GPIO19, Componente1.SDA
  N8: U1.GPIO23, Componente1.SCL
  N9: D1.A, R2.Pin_0

notes:
  CareBox Schematic Hardware
  194087 - André Felipe Rayer Brasil
  178610 - Leonardo Rodrigues Marques
  176121 - Rafael Domingos Nascimento M. Ogallas
  187576 - Thiago Henrique Camargo da Cruz

custom parts:
  ESP32S-30Pin: ESP-WROOM-32 ESP32 ESP-32S Development Board 2.4GHz Dual-Mode WiFi + Bluetooth Dual Cores Microcontroller The ESP32 integrated with Antenna switches, RF Balun, power amplifiers, low-noise amplifiers, filters, and management modules, and the entire solution occupies the least area of PCB. 2.4 GHz Wi-Fi plus Bluetooth dual-mode chip, with TSMC Ultra-low power consumption 40nm technology, power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
