# Fritzing sketch desenho1-178610(1) (saved by Fritzing 0.9.3b)
breadboards: 1

parts:
  Componente2 = Arduino Uno (Rev3)
  LED1 = LED - 5mm [color="Red (633nm)" package="5 mm [THT]"]
  LED2 = LED - 5mm [color="Red (633nm)" package="5 mm [THT]"]
  S1 = Momentary Switch [package=tactile-pth]
  R1 = Photocell (LDR) [package=THT]
  J1 = Piezo Speaker
  R2 = Resistor [tolerance=±5% resistance=10k package="0402 [SMD]"]
  R3 = Resistor [tolerance=±5% resistance=1k package="0402 [SMD]"]
  R4 = Resistor [tolerance=±5% resistance=22 package="0402 [SMD]"]

nets:
  N1: Componente2.A0, R1.pin_1, R2.Pin_0
  N2: Componente2.D9_PWM, R4.Pin_1
  N3: Componente2.D10_PWM/SS, J1.pin2
  N4: Componente2.D2, S1.2
  N5: Componente2.5V, S1.4, R2.Pin_1
  N6: Componente2.GND, LED1.cathode, LED2.cathode, S1.3, R1.pin_0, J1.pin1, R3.Pin_0, R3.Pin_1
  N7: LED1.anode, LED2.anode, R4.Pin_0

notes:
  Os resistores têm valores diferentes!
  Leonardo Rodrigues Marques - 178610.
